// Logisim project project1.circ as structural Verilog
module _4 (
  input  [31:0] in_1,
  output [31:0] out_2
);

  // Incrementer incrementer_1: pin names not known; wires that end beside it: in_1[31:2], out_2[31:2]

  assign out_2[1:0] = in_1[1:0];
endmodule

module Fetch (
  input  [31:0] JI,
  input  [31:0] JR,
  input  [31:0] BranchTarget,
  input  Clock,
  input  Is_Branch,
  input  Is_JI,
  input  Is_JR,
  input  [31:0] Ex_D,
  input  NOP,
  output [31:0] RomIn,
  output [31:0] PC_4
);

  wire and_1_out;
  wire [31:0] multiplexer_1_out, multiplexer_2_out, multiplexer_3_out, multiplexer_4_out, multiplexer_5_out,
       multiplexer_6_out;

  Register #(.width(32)) register_1 (.D(multiplexer_6_out), .Q(RomIn), .clk(Clock));  // open: en, clr
  _4 u_4_1 (.in_1(RomIn), .out_2(PC_4));
  Multiplexer #(.width(32), .enable("false")) multiplexer_1 (
    .in0(PC_4), .in1({PC_4[31:28], JI[25:0], 2'b00}), .out(multiplexer_1_out), .sel(Is_JI));
  Multiplexer #(.width(32), .enable("false")) multiplexer_2 (
    .in0(PC_4), .in1(JR), .out(multiplexer_2_out), .sel(Is_JR));
  Multiplexer #(.width(32), .enable("false")) multiplexer_3 (
    .in0(multiplexer_1_out), .in1(multiplexer_2_out), .out(multiplexer_3_out), .sel(Is_JR));
  Multiplexer #(.width(32), .enable("false")) multiplexer_4 (
    .in0(multiplexer_3_out), .in1(multiplexer_5_out), .out(multiplexer_4_out), .sel(and_1_out));
  Multiplexer #(.width(32), .enable("false")) multiplexer_5 (
    .in0(PC_4), .in1(BranchTarget), .out(multiplexer_5_out), .sel(and_1_out));
  Multiplexer #(.width(32), .enable("false")) multiplexer_6 (
    .in0(multiplexer_4_out), .in1(RomIn), .out(multiplexer_6_out), .sel(NOP));
  and and_1 (and_1_out, Is_Branch, Ex_D[0]);
endmodule

module MIPS32 (
);

  wire clk, Decode_b_or_immediate, Decode_is_branch, Decode_is_jal, Decode_is_jalr, Decode_is_r, Decode_l_s,
       Decode_lt_ge, Decode_mem, Decode_memsel, Decode_sign_unsign, Decode_weirdbranch, Decode_whichsa,
       Decode_writeen, Ex_MEM_l_s_2, Ex_MEM_mem_2, Ex_MEM_memsel_2, Ex_MEM_sign_unsign_2, Ex_Mem_WE, Ex_WE,
       Execute_l_s_2, Execute_mem_out, Execute_memsel_2, Execute_sign_unsign_2, Execute_zap, ID_EX_b_or_imm,
       ID_EX_is_branch_2, ID_EX_is_jal_2, ID_EX_is_jalr_2, ID_EX_is_r, ID_EX_l_s_2, ID_EX_lt_ge_2,
       ID_EX_mem_2, ID_EX_memsel_2, ID_EX_sign_unsign_2, ID_EX_we_2, ID_EX_weirdbranch_2, ID_EX_whichsa_2,
       Is_Branch, Is_JI, Is_JR, MEM_WB_mem_2, Mem_WB_WE, Mem_WE, Memory_mem_out, NOP, NOP_JR, WB_WE, Zap;
  wire [3:0] Decode_alu_op, ID_EX_op_2;
  wire [4:0] Decode_rd, Ex_Mem_Rd, Ex_Rd, ID_EX_rd_2, ID_EX_rs_2, ID_EX_rt_2, Mem_Rd, Mem_WB_Rd, rS, rT,
       WB_Rd;
  wire [31:0] Branch_D, Ex_Mem_D, Ex_MEM_store_2, Execute_store, Fetch_pc_4, Fetch_romin, ID_EX_a_2,
       ID_EX_b_2, ID_EX_imm_2, ID_EX_target, IF_ID_instr, IF_ID_pc_4_2, Imm, JR, MEM_WB_d_2, MEM_WB_m_2,
       Memory_d_2, Memory_m, mipsprogramrom_1_p2, regA, regB, Target, WB_D;

  Clock Clock (.out(clk));
  Fetch Fetch (
    .RomIn(Fetch_romin), .Clock(clk), .BranchTarget(Target), .Is_JI(Is_JI), .PC_4(Fetch_pc_4), .JR(JR),
    .JI(Imm), .Is_JR(Is_JR), .Ex_D(Branch_D), .Is_Branch(Is_Branch), .NOP(NOP));
  // Probe on WB_D
  // MIPSProgramROM mipsprogramrom_1: pin names not known; wires that end beside it: Fetch_romin, mipsprogramrom_1_p2, clk, WB_WE
  IF_DE IF_ID (.InstrIn(mipsprogramrom_1_p2), .PC_4(Fetch_pc_4), .clk(clk), .Instr(IF_ID_instr), .PC_4_2(IF_ID_pc_4_2));
  Decode Decode (
    .Op(IF_ID_instr), .whichSa(Decode_whichsa), .WriteEn(Decode_writeen), .Rs(rS), .Rt(rT),
    .ALU_Op(Decode_alu_op), .Rd(Decode_rd), .MemSel(Decode_memsel), .B_or_Immediate(Decode_b_or_immediate),
    .Immediate(Imm), .Is_R(Decode_is_r), .Mem(Decode_mem), .Sign_Unsign(Decode_sign_unsign),
    .L_S(Decode_l_s), .Is_JR(Is_JR), .Is_JI(Is_JI), .Is_JAL(Decode_is_jal), .Is_JALR(Decode_is_jalr),
    .LT_GE(Decode_lt_ge), .Is_Branch(Decode_is_branch), .WeirdBranch(Decode_weirdbranch), .Zap(Zap),
    .Clock(clk), .NOP_JR(NOP_JR));
  // RegisterFile registerfile_1: pin names not known; wires that end beside it: WB_D, WB_Rd, rS, rT, regA, regB
  ID_EX ID_EX (
    .A(regA), .B(regB), .whichSA(Decode_whichsa), .WE(Decode_writeen), .Rs(rS), .Rt(rT), .Op(Decode_alu_op),
    .Rd(Decode_rd), .MemSel(Decode_memsel), .B_or_Immediate(Decode_b_or_immediate), .Imm(Imm),
    .isR(Decode_is_r), .Mem(Decode_mem), .L_S(Decode_l_s), .PC_4(IF_ID_pc_4_2), .A_2(ID_EX_a_2),
    .B_2(ID_EX_b_2), .whichSA_2(ID_EX_whichsa_2), .WE_2(ID_EX_we_2), .Rs_2(ID_EX_rs_2), .Rt_2(ID_EX_rt_2),
    .Op_2(ID_EX_op_2), .Rd_2(ID_EX_rd_2), .MemSel_2(ID_EX_memsel_2), .B_or_Imm(ID_EX_b_or_imm),
    .Imm_2(ID_EX_imm_2), .is_R(ID_EX_is_r), .Mem_2(ID_EX_mem_2), .L_S_2(ID_EX_l_s_2), .target(ID_EX_target),
    .clk(clk), .Sign_Unsign(Decode_sign_unsign), .Sign_Unsign_2(ID_EX_sign_unsign_2),
    .Is_JAL_2(ID_EX_is_jal_2), .Is_JAL(Decode_is_jal), .Is_JALR_2(ID_EX_is_jalr_2), .Is_JALR(Decode_is_jalr),
    .LT_GE_2(ID_EX_lt_ge_2), .LT_GE(Decode_lt_ge), .Is_Branch_2(ID_EX_is_branch_2),
    .Is_Branch(Decode_is_branch), .WeirdBranch_2(ID_EX_weirdbranch_2), .WeirdBranch(Decode_weirdbranch),
    .Ex_D(Branch_D), .WB_D(WB_D), .Ex_WE(Ex_WE), .Ex_Rd(Ex_Rd), .WB_WE(WB_WE), .WB_Rd(WB_Rd), .M_WE(Mem_WE),
    .M_Rd(Mem_Rd), .Is_JR(Is_JR), .NOP(NOP), .JR(JR), .NOP_JR(NOP_JR));
  Execute Execute (
    .Rt(ID_EX_rt_2), .A(ID_EX_a_2), .Rd(ID_EX_rd_2), .Is_R(ID_EX_is_r), .Mem_D(Ex_Mem_D), .WB_D(WB_D),
    .ALU_Op(ID_EX_op_2), .Immediate(ID_EX_imm_2), .B(ID_EX_b_2), .whichSA(ID_EX_whichsa_2), .WE(ID_EX_we_2),
    .Ex_Mem_WE(Ex_Mem_WE), .B_or_Immediate(ID_EX_b_or_imm), .Mem_WB_WE(Mem_WB_WE), .Mem_WB_Rd(Mem_WB_Rd),
    .MemSel(ID_EX_memsel_2), .L_S(ID_EX_l_s_2), .Mem_in(ID_EX_mem_2), .PC_4(ID_EX_target),
    .Sign_Unsign(ID_EX_sign_unsign_2), .Dest(Ex_Rd), .D(Branch_D), .WE2(Ex_WE), .MemSel_2(Execute_memsel_2),
    .L_S_2(Execute_l_s_2), .Mem_out(Execute_mem_out), .target(Target), .Sign_Unsign_2(Execute_sign_unsign_2),
    .Rs(ID_EX_rs_2), .Store(Execute_store), .Ex_Mem_Rd(Ex_Mem_Rd), .Is_JAL(ID_EX_is_jal_2),
    .Is_JALR(ID_EX_is_jalr_2), .LT_GE(ID_EX_lt_ge_2), .Is_Branch(ID_EX_is_branch_2), .Is_Branch_2(Is_Branch),
    .WeirdBranch(ID_EX_weirdbranch_2), .Zap(Execute_zap));
  EX_MEM Ex_MEM (
    .Dest(Ex_Rd), .Store(Execute_store), .D(Branch_D), .WE(Ex_WE), .MemSel(Execute_memsel_2),
    .L_S(Execute_l_s_2), .Mem(Execute_mem_out), .target(Target), .Dest_2(Ex_Mem_Rd),
    .Store_2(Ex_MEM_store_2), .D_2(Ex_Mem_D), .WE_2(Ex_Mem_WE), .MemSel_2(Ex_MEM_memsel_2),
    .L_S_2(Ex_MEM_l_s_2), .Mem_2(Ex_MEM_mem_2), .clk(clk), .Sign_Unsign_2(Ex_MEM_sign_unsign_2),
    .Sign_Unsign(Execute_sign_unsign_2), .Zap_2(Zap), .Zap(Execute_zap));  // open: target_2
  Memory Memory (
    .Dest(Ex_Mem_Rd), .Mem_in(Ex_MEM_mem_2), .WE(Ex_Mem_WE), .Store(Ex_MEM_store_2), .L_S(Ex_MEM_l_s_2),
    .D(Ex_Mem_D), .Sign_Unsign(Ex_MEM_sign_unsign_2), .MemSel(Ex_MEM_memsel_2), .Dest_2(Mem_Rd),
    .Mem_out(Memory_mem_out), .WE_2(Mem_WE), .D_2(Memory_d_2), .Clock(clk), .M(Memory_m));
  MEM_WB MEM_WB (
    .Dest(Mem_Rd), .Mem(Memory_mem_out), .WE(Mem_WE), .M(Memory_m), .D(Memory_d_2), .Dest_2(Mem_WB_Rd),
    .Mem_2(MEM_WB_mem_2), .WE_2(Mem_WB_WE), .M_2(MEM_WB_m_2), .D_2(MEM_WB_d_2), .clk(clk));
  Writeback WriteBack (
    .Dest(Mem_WB_Rd), .Mem(MEM_WB_mem_2), .WE(Mem_WB_WE), .D(MEM_WB_d_2), .M(MEM_WB_m_2), .rW(WB_Rd),
    .WE_2(WB_WE), .D_2(WB_D));

  // Other names for the same wires on the sheet: Ex_D[31:0] = Branch_D
endmodule

module Immediate_Decode (
  input  IsR,
  input  [31:0] Op,
  output BorImmediate,
  output [31:0] Immediate
);

  wire and_1_out, and_2_out, and_3_out, not_1_out, not_2_out, not_3_out, not_4_out, not_5_out, or_1_out;
  wire [31:0] bit_extender_1_out, bit_extender_2_out;

  not not_1 (not_1_out, Op[31]);
  and and_1 (and_1_out, not_1_out, not_2_out, not_3_out);
  not not_2 (not_2_out, Op[29]);
  not not_3 (not_3_out, Op[27]);
  not not_4 (not_4_out, Op[31]);
  and and_2 (and_2_out, not_4_out, not_5_out, Op[28]);
  not not_5 (not_5_out, Op[29]);
  or or_1 (or_1_out, and_1_out, and_2_out);
  or or_2 (BorImmediate, or_1_out, IsR);
  and and_3 (and_3_out, Op[28], Op[29]);
  assign bit_extender_1_out = {{16{Op[15]}}, Op[15:0]};  // Bit_Extender bit_extender_1
  assign bit_extender_2_out = {{16{1'b0}}, Op[15:0]};  // Bit_Extender bit_extender_2
  Multiplexer #(.width(32), .enable("false")) multiplexer_1 (
    .in0(bit_extender_1_out), .in1(bit_extender_2_out), .out(Immediate), .sel(and_3_out));
endmodule

module Non_Immediate_Decode (
  input  [31:0] Op,
  output Enable,
  output Is_JR,
  output IS_JALR,
  output whichSA,
  output [4:0] rd,
  output LT_GE,
  output [4:0] rt,
  output [4:0] rs,
  output Memory,
  output [3:0] Control,
  output L_S,
  output Sign_Unsign,
  output MemSel,
  output IsR,
  output Is_Branch,
  output WeirdBranch,
  output Is_JAL,
  output Is_JI
);

  wire and_7_out, and_8_out, and_11_out, and_12_out, and_13_out;
  wire [3:0] rom_1_data, rom_2_data;

  and and_1 (MemSel, Op[27], Op[26]);
  and and_2 (WeirdBranch, Is_Branch, ~Op[28]);  // AND_Gate
  and and_3 (Is_JI, ~Op[31], ~Op[30], ~Op[29], ~Op[28], Op[27]);  // AND_Gate
  and and_4 (whichSA, Op[2], IsR);
  nor nor_1 (Is_Branch, Op[29], Op[31], IsR);
  and and_5 (Is_JAL, Op[26], Is_JI);
  and and_6 (Is_JR, IsR, and_7_out);
  and and_7 (and_7_out, ~Op[5], ~Op[4], Op[3], ~Op[2], ~Op[1]);  // AND_Gate
  and and_8 (and_8_out, Is_Branch, ~Is_JAL);  // AND_Gate
  and and_9 (IS_JALR, Is_JR, Op[0]);
  and and_10 (IsR, ~Op[26], ~Op[27], ~Op[28], ~Op[29], ~Op[30], ~Op[31]);  // AND_Gate
  ROM #(.addrWidth(5), .dataWidth(4)) rom_1 (.addr({Op[31], Op[29:26]}), .data(rom_1_data));  // open: sel
  and and_11 (and_11_out, Op[29], Op[31]);
  ROM #(.addrWidth(5), .dataWidth(4)) rom_2 (.addr({Op[5], Op[3:0]}), .data(rom_2_data));  // open: sel
  and and_12 (and_12_out, Is_JR, ~IS_JALR);  // AND_Gate
  and and_13 (and_13_out, Is_JI, ~Is_JAL);  // AND_Gate
  Multiplexer #(.width(4), .enable("false")) multiplexer_1 (
    .in0(rom_1_data), .in1(rom_2_data), .out(Control), .sel(IsR));
  and and_14 (Enable, ~and_11_out, ~and_8_out, ~and_12_out, ~and_13_out);  // AND_Gate

  assign L_S = Op[29];
  assign LT_GE = Op[16];
  assign Memory = Op[31];
  assign rd = Op[15:11];
  assign rs = Op[25:21];
  assign rt = Op[20:16];
  assign Sign_Unsign = Op[28];

  // Other names for the same wires on the sheet: Is_Store = Op[29]; Mem = Op[31]; Is_JALI = Is_JAL

  // Notes on the sheet:
  //   contents of rom_1 (hex, n*v repeats v):
  //   0 d 0 0 9 b f d 0 2 f 7 8 a c 1 2 0 0 2 2 0 0 0 2 0 0 2
  //   contents of rom_2 (hex, n*v repeats v):
  //   0 0 4 5 0 0 4 5 0 0 9 b 5*0 2 0 6 8 a c e 0 0 f 7
endmodule

module Memory (
  input  [4:0] Dest,
  input  Mem_in,
  input  WE,
  input  [31:0] Store,
  input  Clock,
  input  L_S,
  input  Sign_Unsign,
  input  [31:0] D,
  input  MemSel,
  output [4:0] Dest_2,
  output Mem_out,
  output WE_2,
  output [31:0] M,
  output [31:0] D_2
);

  wire not_1_out, not_2_out, not_3_out, not_4_out, not_5_out;
  wire [3:0] and_4_out, bit_extender_15_out, Sel;
  wire [7:0] bit_extender_3_out;
  wire [15:0] bit_extender_4_out, bit_extender_5_out;
  wire [23:0] bit_extender_2_out, bit_extender_6_out;
  wire [31:0] bit_extender_1_out, bit_extender_7_out, bit_extender_8_out, bit_extender_9_out,
       bit_extender_10_out, bit_extender_11_out, bit_extender_12_out, bit_extender_13_out,
       bit_extender_14_out, mips_ram_1_p7, multiplexer_1_out, multiplexer_2_out, multiplexer_4_out,
       multiplexer_5_out, multiplexer_6_out;

  assign bit_extender_1_out = {{24{1'b0}}, Store[7:0]};  // Bit_Extender bit_extender_1
  assign bit_extender_2_out = {{16{1'b0}}, Store[7:0]};  // Bit_Extender bit_extender_2
  assign bit_extender_3_out = {{7{1'b0}}, 1'b0};  // Bit_Extender bit_extender_3
  assign bit_extender_4_out = {{8{1'b0}}, Store[7:0]};  // Bit_Extender bit_extender_4
  assign bit_extender_5_out = {{15{1'b0}}, 1'b0};  // Bit_Extender bit_extender_5
  assign bit_extender_6_out = {{23{1'b0}}, 1'b0};  // Bit_Extender bit_extender_6
  Multiplexer #(.select(2), .width(32), .enable("false")) multiplexer_1 (
    .in0(bit_extender_1_out), .in1({bit_extender_2_out, bit_extender_3_out}),
    .in2({bit_extender_4_out, bit_extender_5_out}), .in3({Store[7:0], bit_extender_6_out}),
    .out(multiplexer_1_out), .sel(D[1:0]));
  Multiplexer #(.width(32), .enable("false")) multiplexer_2 (
    .in0(multiplexer_1_out), .in1(Store), .out(multiplexer_2_out), .sel(MemSel));
  and and_1 (and_4_out[3], D[1], D[0]);
  not not_1 (not_1_out, D[0]);
  not not_2 (not_2_out, D[1]);
  not not_3 (not_3_out, D[1]);
  not not_4 (not_4_out, D[0]);
  not not_5 (not_5_out, L_S);
  and and_2 (and_4_out[2], D[1], not_1_out);
  and and_3 (and_4_out[1], not_2_out, D[0]);
  and and_4 (and_4_out[0], not_3_out, not_4_out);
  // MIPS_RAM mips_ram_1: pin names not known; wires that end beside it: D[21:2], multiplexer_2_out, L_S, Sel, Clock, not_5_out, mips_ram_1_p7
  assign bit_extender_7_out = {{24{1'b0}}, mips_ram_1_p7[7:0]};  // Bit_Extender bit_extender_7
  assign bit_extender_8_out = {{24{mips_ram_1_p7[7]}}, mips_ram_1_p7[7:0]};  // Bit_Extender bit_extender_8
  assign bit_extender_9_out = {{24{1'b0}}, mips_ram_1_p7[15:8]};  // Bit_Extender bit_extender_9
  assign bit_extender_10_out = {{24{mips_ram_1_p7[15]}}, mips_ram_1_p7[15:8]};  // Bit_Extender bit_extender_10
  assign bit_extender_11_out = {{24{1'b0}}, mips_ram_1_p7[23:16]};  // Bit_Extender bit_extender_11
  assign bit_extender_12_out = {{24{mips_ram_1_p7[23]}}, mips_ram_1_p7[23:16]};  // Bit_Extender bit_extender_12
  assign bit_extender_13_out = {{24{1'b0}}, mips_ram_1_p7[31:24]};  // Bit_Extender bit_extender_13
  assign bit_extender_14_out = {{24{mips_ram_1_p7[31]}}, mips_ram_1_p7[31:24]};  // Bit_Extender bit_extender_14
  assign bit_extender_15_out = {{3{MemSel}}, MemSel};  // Bit_Extender bit_extender_15
  Multiplexer #(.width(4), .enable("false")) multiplexer_3 (
    .in0(and_4_out), .in1(bit_extender_15_out), .out(Sel), .sel(MemSel));
  Multiplexer #(.select(2), .width(32), .enable("false")) multiplexer_4 (
    .in0(bit_extender_7_out), .in1(bit_extender_9_out), .in2(bit_extender_11_out), .in3(bit_extender_13_out),
    .out(multiplexer_4_out), .sel(D[1:0]));
  Multiplexer #(.select(2), .width(32), .enable("false")) multiplexer_5 (
    .in0(bit_extender_8_out), .in1(bit_extender_10_out), .in2(bit_extender_12_out),
    .in3(bit_extender_14_out), .out(multiplexer_5_out), .sel(D[1:0]));
  Multiplexer #(.width(32), .enable("false")) multiplexer_6 (
    .in0(multiplexer_5_out), .in1(multiplexer_4_out), .out(multiplexer_6_out), .sel(Sign_Unsign));
  Multiplexer #(.width(32), .enable("false")) multiplexer_7 (
    .in0(multiplexer_6_out), .in1(mips_ram_1_p7), .out(M), .sel(MemSel));

  assign D_2 = D;
  assign Dest_2 = Dest;
  assign Mem_out = Mem_in;
  assign WE_2 = WE;
endmodule

module Writeback (
  input  [4:0] Dest,
  input  Mem,
  input  WE,
  input  [31:0] D,
  input  [31:0] M,
  output [4:0] rW,
  output WE_2,
  output [31:0] D_2
);

  Multiplexer #(.width(32), .enable("false")) multiplexer_1 (.in0(D), .in1(M), .out(D_2), .sel(Mem));

  assign rW = Dest;
  assign WE_2 = WE;
endmodule

module IF_DE (
  input  [31:0] InstrIn,
  input  [31:0] PC_4,
  input  clk,
  output [31:0] Instr,
  output [31:0] PC_4_2
);

  Register #(.width(32)) register_1 (.D(InstrIn), .Q(Instr), .clk(clk));  // open: en, clr
  Register #(.width(32)) register_2 (.D(PC_4), .Q(PC_4_2), .clk(clk));  // open: en, clr
endmodule

module EX_MEM (
  input  [4:0] Dest,
  input  [31:0] Store,
  input  [31:0] D,
  input  WE,
  input  MemSel,
  input  L_S,
  input  Mem,
  input  [31:0] target,
  input  Sign_Unsign,
  input  Zap,
  input  clk,
  output [4:0] Dest_2,
  output [31:0] Store_2,
  output [31:0] D_2,
  output WE_2,
  output MemSel_2,
  output L_S_2,
  output Mem_2,
  output [31:0] target_2,
  output Sign_Unsign_2,
  output Zap_2
);

  Register #(.width(5)) u_Dest (.D(Dest), .Q(Dest_2), .clk(clk));  // open: en, clr
  Register #(.width(32)) u_Store (.D(Store), .Q(Store_2), .clk(clk));  // open: en, clr
  Register #(.width(32)) u_D (.D(D), .Q(D_2), .clk(clk));  // open: en, clr
  Register #(.width(32)) register_1 (.D(target), .Q(target_2), .clk(clk));  // open: en, clr
  D_Flip_Flop u_WE (.clk(clk), .D(WE), .Q(WE_2));  // open: Qn, preset, en, reset
  D_Flip_Flop u_MemSel (.clk(clk), .D(MemSel), .Q(MemSel_2));  // open: Qn, preset, en, reset
  D_Flip_Flop u_L_S (.clk(clk), .D(L_S), .Q(L_S_2));  // open: Qn, preset, en, reset
  D_Flip_Flop u_Mem (.clk(clk), .D(Mem), .Q(Mem_2));  // open: Qn, preset, en, reset
  D_Flip_Flop u_Sign_Unsign (.clk(clk), .D(Sign_Unsign), .Q(Sign_Unsign_2));  // open: Qn, preset, en, reset
  D_Flip_Flop u_Zap (.clk(clk), .D(Zap), .Q(Zap_2));  // open: Qn, preset, en, reset
endmodule

module MEM_WB (
  input  [4:0] Dest,
  input  Mem,
  input  WE,
  input  [31:0] M,
  input  [31:0] D,
  input  clk,
  output [4:0] Dest_2,
  output Mem_2,
  output WE_2,
  output [31:0] M_2,
  output [31:0] D_2
);

  Register #(.width(5)) register_1 (.D(Dest), .Q(Dest_2), .clk(clk));  // open: en, clr
  D_Flip_Flop d_ff_1 (.clk(clk), .D(Mem), .Q(Mem_2));  // open: Qn, preset, en, reset
  D_Flip_Flop d_ff_2 (.clk(clk), .D(WE), .Q(WE_2));  // open: Qn, preset, en, reset
  Register #(.width(32)) register_2 (.D(M), .Q(M_2), .clk(clk));  // open: en, clr
  Register #(.width(32)) register_3 (.D(D), .Q(D_2), .clk(clk));  // open: en, clr
endmodule

module EqZero (
  input  [31:0] A,
  output EqZ
);

  and and_1 (EqZ, ~A[0], ~A[1], ~A[2], ~A[3], ~A[4], ~A[5], ~A[6], ~A[7], ~A[8], ~A[9], ~A[10], ~A[11], ~A[12], ~A[13], ~A[14], ~A[15], ~A[16], ~A[17], ~A[18], ~A[19], ~A[20], ~A[21], ~A[22], ~A[23], ~A[24], ~A[25], ~A[26], ~A[27], ~A[28], ~A[29], ~A[30], ~A[31]);  // AND_Gate
endmodule

module Forwarding_Unit (
  input  [4:0] Id_Ex_Ra_b,
  input  Ex_M_We,
  input  [4:0] Ex_M_Rd,
  input  M_WB_We,
  input  [4:0] M_Wb_Rd,
  output [1:0] Forward
);

  Ex_Mem_Bypass ex_mem_bypass_1 (.Ex_M_We(Ex_M_We), .Ex_M_Rd(Ex_M_Rd), .Id_Ex_Ra_b(Id_Ex_Ra_b), .Forward(Forward[0]));
  Mem_WB_Bypass mem_wb_bypass_1 (
    .M_WB_WE(M_WB_We), .M_WB_Rd(M_Wb_Rd), .Id_Ex_Ra_b(Id_Ex_Ra_b), .Ex_Mem_We(Ex_M_We), .Ex_M_Rd(Ex_M_Rd),
    .Forward(Forward[1]));
endmodule

module Ex_Mem_Bypass (
  input  Ex_M_We,
  input  [4:0] Ex_M_Rd,
  input  [4:0] Id_Ex_Ra_b,
  output Forward
);

  wire and_1_out, or_1_out;
  wire [4:0] not_1_out, xor_1_out;

  or or_1 (or_1_out, Ex_M_Rd[0], Ex_M_Rd[1], Ex_M_Rd[2], Ex_M_Rd[3], Ex_M_Rd[4]);
  assign xor_1_out = Ex_M_Rd ^ Id_Ex_Ra_b;  // XOR_Gate xor_1, 5 bits wide
  assign not_1_out = ~xor_1_out;  // NOT_Gate not_1, 5 bits wide
  and and_1 (and_1_out, not_1_out[0], not_1_out[1], not_1_out[2], not_1_out[3], not_1_out[4]);
  and and_2 (Forward, Ex_M_We, or_1_out, and_1_out);
endmodule

module Mem_WB_Bypass (
  input  M_WB_WE,
  input  [4:0] M_WB_Rd,
  input  [4:0] Id_Ex_Ra_b,
  input  Ex_Mem_We,
  input  [4:0] Ex_M_Rd,
  output Forward
);

  wire ex_mem_bypass_1_forward, ex_mem_bypass_2_forward;

  Ex_Mem_Bypass ex_mem_bypass_1 (
    .Ex_M_We(M_WB_WE), .Ex_M_Rd(M_WB_Rd), .Id_Ex_Ra_b(Id_Ex_Ra_b), .Forward(ex_mem_bypass_1_forward));
  Ex_Mem_Bypass ex_mem_bypass_2 (
    .Ex_M_We(Ex_Mem_We), .Ex_M_Rd(Ex_M_Rd), .Id_Ex_Ra_b(Id_Ex_Ra_b), .Forward(ex_mem_bypass_2_forward));
  and and_1 (Forward, ex_mem_bypass_1_forward, ~ex_mem_bypass_2_forward);  // AND_Gate
endmodule

module ID_EX (
  input  [31:0] A,
  input  [31:0] Ex_D,
  input  [31:0] B,
  input  [31:0] WB_D,
  input  Ex_WE,
  input  [4:0] Ex_Rd,
  input  whichSA,
  input  M_WE,
  input  [4:0] M_Rd,
  input  WB_WE,
  input  [4:0] WB_Rd,
  input  Is_JR,
  input  WE,
  input  [4:0] Rs,
  input  [4:0] Rt,
  input  [3:0] Op,
  input  [4:0] Rd,
  input  MemSel,
  input  B_or_Immediate,
  input  [31:0] Imm,
  input  isR,
  input  Mem,
  input  L_S,
  input  Sign_Unsign,
  input  [31:0] PC_4,
  input  Is_JAL,
  input  Is_JALR,
  input  LT_GE,
  input  Is_Branch,
  input  WeirdBranch,
  input  clk,
  output [31:0] JR,
  output [31:0] A_2,
  output [31:0] B_2,
  output whichSA_2,
  output WE_2,
  output [4:0] Rs_2,
  output NOP,
  output [4:0] Rt_2,
  output [3:0] Op_2,
  output [4:0] Rd_2,
  output MemSel_2,
  output B_or_Imm,
  output [31:0] Imm_2,
  output is_R,
  output Mem_2,
  output L_S_2,
  output Sign_Unsign_2,
  output [31:0] target,
  output Is_JAL_2,
  output Is_JALR_2,
  output LT_GE_2,
  output Is_Branch_2,
  output WeirdBranch_2,
  output NOP_JR
);

  wire and_1_out, and_2_out, eqzero5_1_eqz, eqzero5_2_eqz, ex_mem_bypass_1_forward, ex_mem_bypass_2_forward,
       jump_forwarding_1_nop, LoadUseHazard, multiplexer_5_out, multiplexer_6_out, multiplexer_11_out,
       multiplexer_12_out, multiplexer_14_out, multiplexer_15_out, multiplexer_16_out, multiplexer_17_out,
       multiplexer_18_out, multiplexer_19_out, multiplexer_20_out, multiplexer_21_out, multiplexer_22_out,
       multiplexer_23_out, or_2_out, or_3_out;
  wire [1:0] jump_forwarding_1_forward;
  wire [3:0] multiplexer_9_out;
  wire [4:0] multiplexer_7_out, multiplexer_8_out, multiplexer_10_out;
  wire [31:0] multiplexer_2_out, multiplexer_3_out, multiplexer_4_out, multiplexer_13_out, n4_1_out_2;

  Jump_Forwarding jump_forwarding_1 (
    .Ex_M_We(Ex_WE), .Ex_M_Rd(Ex_Rd), .M_WB_We(M_WE), .M_Wb_Rd(M_Rd), .WB_We(WB_WE), .Wb_Rd(WB_Rd),
    .Forward(jump_forwarding_1_forward), .Id_Ex_Ra_b(Rs), .NOP(jump_forwarding_1_nop), .Is_JR(Is_JR));
  or or_1 (NOP, jump_forwarding_1_nop, LoadUseHazard);
  Multiplexer #(.select(2), .width(32), .enable("false")) multiplexer_1 (
    .in0(A), .in1(Ex_D), .in2(WB_D), .in3(Ex_D), .out(JR), .sel(jump_forwarding_1_forward));
  _4 u_4_1 (.in_1(PC_4), .out_2(n4_1_out_2));
  Multiplexer #(.width(32), .enable("false")) multiplexer_2 (
    .in0(n4_1_out_2), .in1(PC_4), .out(multiplexer_2_out), .sel(or_2_out));
  or or_2 (or_2_out, NOP_JR, Is_Branch);
  Multiplexer #(.width(32), .enable("false")) multiplexer_3 (
    .in0(JR), .in1({32{1'b0}}), .out(multiplexer_3_out), .sel(NOP));
  Multiplexer #(.width(32), .enable("false")) multiplexer_4 (
    .in0(B), .in1({32{1'b0}}), .out(multiplexer_4_out), .sel(NOP));
  Multiplexer #(.enable("false")) multiplexer_5 (.in0(whichSA), .in1(1'b0), .out(multiplexer_5_out), .sel(NOP));
  Multiplexer #(.enable("false")) multiplexer_6 (.in0(WE), .in1(1'b0), .out(multiplexer_6_out), .sel(NOP));
  Multiplexer #(.width(5), .enable("false")) multiplexer_7 (
    .in0(Rs), .in1({5{1'b0}}), .out(multiplexer_7_out), .sel(NOP));
  Multiplexer #(.width(5), .enable("false")) multiplexer_8 (
    .in0(Rt), .in1({5{1'b0}}), .out(multiplexer_8_out), .sel(NOP));
  Multiplexer #(.width(4), .enable("false")) multiplexer_9 (
    .in0(Op), .in1(4'b0000), .out(multiplexer_9_out), .sel(NOP));
  Multiplexer #(.width(5), .enable("false")) multiplexer_10 (
    .in0(Rd), .in1({5{1'b0}}), .out(multiplexer_10_out), .sel(NOP));
  Multiplexer #(.enable("false")) multiplexer_11 (.in0(MemSel), .in1(1'b0), .out(multiplexer_11_out), .sel(NOP));
  Multiplexer #(.enable("false")) multiplexer_12 (
    .in0(B_or_Immediate), .in1(1'b1), .out(multiplexer_12_out), .sel(NOP));
  Multiplexer #(.width(32), .enable("false")) multiplexer_13 (
    .in0(Imm), .in1({32{1'b0}}), .out(multiplexer_13_out), .sel(NOP));
  Multiplexer #(.enable("false")) multiplexer_14 (.in0(isR), .in1(1'b1), .out(multiplexer_14_out), .sel(NOP));
  Multiplexer #(.enable("false")) multiplexer_15 (.in0(Mem), .in1(1'b0), .out(multiplexer_15_out), .sel(NOP));
  Multiplexer #(.enable("false")) multiplexer_16 (.in0(L_S), .in1(1'b0), .out(multiplexer_16_out), .sel(NOP));
  Multiplexer #(.enable("false")) multiplexer_17 (.in0(Sign_Unsign), .in1(1'b0), .out(multiplexer_17_out), .sel(NOP));
  Multiplexer #(.enable("false")) multiplexer_18 (.in0(Is_JAL), .in1(1'b0), .out(multiplexer_18_out), .sel(NOP));
  Multiplexer #(.enable("false")) multiplexer_19 (.in0(Is_JALR), .in1(1'b0), .out(multiplexer_19_out), .sel(NOP));
  Multiplexer #(.enable("false")) multiplexer_20 (.in0(LT_GE), .in1(1'b0), .out(multiplexer_20_out), .sel(NOP));
  Multiplexer #(.enable("false")) multiplexer_21 (.in0(Is_Branch), .in1(1'b0), .out(multiplexer_21_out), .sel(NOP));
  Multiplexer #(.enable("false")) multiplexer_22 (.in0(WeirdBranch), .in1(1'b0), .out(multiplexer_22_out), .sel(NOP));
  Register #(.width(32)) u_A (.D(multiplexer_3_out), .Q(A_2), .clk(clk));  // open: en, clr
  Register #(.width(32)) u_B (.D(multiplexer_4_out), .Q(B_2), .clk(clk));  // open: en, clr
  D_Flip_Flop u_whichSA (.clk(clk), .D(multiplexer_5_out), .Q(whichSA_2));  // open: Qn, preset, en, reset
  D_Flip_Flop u_WE (.clk(clk), .D(multiplexer_6_out), .Q(WE_2));  // open: Qn, preset, en, reset
  Register #(.width(5)) u_Rs (.D(multiplexer_7_out), .Q(Rs_2), .clk(clk));  // open: en, clr
  Register #(.width(5)) u_Rt (.D(multiplexer_8_out), .Q(Rt_2), .clk(clk));  // open: en, clr
  Register #(.width(4)) u_Op (.D(multiplexer_9_out), .Q(Op_2), .clk(clk));  // open: en, clr
  Register #(.width(5)) u_Rd (.D(multiplexer_10_out), .Q(Rd_2), .clk(clk));  // open: en, clr
  D_Flip_Flop u_MemSel (.clk(clk), .D(multiplexer_11_out), .Q(MemSel_2));  // open: Qn, preset, en, reset
  D_Flip_Flop u_B_or_immediate (.clk(clk), .D(multiplexer_12_out), .Q(B_or_Imm));  // open: Qn, preset, en, reset
  Register #(.width(32)) u_Imm (.D(multiplexer_13_out), .Q(Imm_2), .clk(clk));  // open: en, clr
  D_Flip_Flop u_Is_R (.clk(clk), .D(multiplexer_14_out), .Q(is_R));  // open: Qn, preset, en, reset
  D_Flip_Flop u_Mem (.clk(clk), .D(multiplexer_15_out), .Q(Mem_2));  // open: Qn, preset, en, reset
  D_Flip_Flop u_L_S (.clk(clk), .D(multiplexer_16_out), .Q(L_S_2));  // open: Qn, preset, en, reset
  D_Flip_Flop u_L_S_2 (.clk(clk), .D(multiplexer_17_out), .Q(Sign_Unsign_2));  // open: Qn, preset, en, reset
  Register #(.width(32)) register_1 (.D(multiplexer_2_out), .Q(target), .clk(clk));  // open: en, clr
  D_Flip_Flop u_Is_JAL (.clk(clk), .D(multiplexer_18_out), .Q(Is_JAL_2));  // open: Qn, preset, en, reset
  D_Flip_Flop u_Is_JALR (.clk(clk), .D(multiplexer_19_out), .Q(Is_JALR_2));  // open: Qn, preset, en, reset
  D_Flip_Flop u_LT_GE (.clk(clk), .D(multiplexer_20_out), .Q(LT_GE_2));  // open: Qn, preset, en, reset
  D_Flip_Flop u_Is_Branch (.clk(clk), .D(multiplexer_21_out), .Q(Is_Branch_2));  // open: Qn, preset, en, reset
  D_Flip_Flop u_WeirdBranch (.clk(clk), .D(multiplexer_22_out), .Q(WeirdBranch_2));  // open: Qn, preset, en, reset
  D_Flip_Flop u_NOP (.clk(clk), .D(NOP), .Q(NOP_JR));  // open: Qn, preset, en, reset
  and and_1 (and_1_out, Mem_2, ~L_S_2);  // AND_Gate
  Ex_Mem_Bypass ex_mem_bypass_1 (.Ex_M_We(WE_2), .Ex_M_Rd(Rt_2), .Id_Ex_Ra_b(Rt), .Forward(ex_mem_bypass_1_forward));
  Ex_Mem_Bypass ex_mem_bypass_2 (.Ex_M_We(WE_2), .Ex_M_Rd(Rt_2), .Id_Ex_Ra_b(Rs), .Forward(ex_mem_bypass_2_forward));
  or or_3 (or_3_out, ex_mem_bypass_2_forward, ex_mem_bypass_1_forward);
  EqZero5 eqzero5_1 (.A(Rt), .EqZ(eqzero5_1_eqz));
  and and_2 (and_2_out, or_3_out, ~multiplexer_23_out);  // AND_Gate
  EqZero5 eqzero5_2 (.A(Rd), .EqZ(eqzero5_2_eqz));
  Multiplexer #(.enable("false")) multiplexer_23 (
    .in0(eqzero5_1_eqz), .in1(eqzero5_2_eqz), .out(multiplexer_23_out), .sel(isR));
  and and_3 (LoadUseHazard, and_2_out, and_1_out);

  // Other names for the same wires on the sheet: Ra[4:0] = Rs; Rb[4:0] = Rt
endmodule

module Execute (
  input  [4:0] Rt,
  input  [4:0] Rd,
  input  LT_GE,
  input  [31:0] A,
  input  Is_Branch,
  input  Is_R,
  input  [31:0] Mem_D,
  input  WeirdBranch,
  input  [31:0] WB_D,
  input  [3:0] ALU_Op,
  input  [31:0] Immediate,
  input  Is_JAL,
  input  [31:0] B,
  input  whichSA,
  input  Is_JALR,
  input  [4:0] Rs,
  input  Ex_Mem_WE,
  input  B_or_Immediate,
  input  WE,
  input  [4:0] Ex_Mem_Rd,
  input  Mem_WB_WE,
  input  [4:0] Mem_WB_Rd,
  input  MemSel,
  input  L_S,
  input  Mem_in,
  input  [31:0] PC_4,
  input  Sign_Unsign,
  output [4:0] Dest,
  output Is_Branch_2,
  output [31:0] Store,
  output [31:0] D,
  output Zap,
  output WE2,
  output [31:0] target,
  output MemSel_2,
  output L_S_2,
  output Mem_out,
  output Sign_Unsign_2
);

  wire and_2_out, comparator_1_lt, comparator_2_lt, eq_ne_cmd, eqzero_1_eqz, MOVx, multiplexer_3_out,
       not_1_out, or_1_out, or_2_out, or_3_out, SLTx, xor_1_out;
  wire [1:0] forwarding_unit_1_forward, forwarding_unit_2_forward;
  wire [4:0] mips_alu_1_p4, multiplexer_6_out;
  wire [31:0] A_t, bit_extender_2_out, bit_extender_3_out, bit_extender_4_out, LTGEOut, mips_alu_1_p5,
       multiplexer_4_out, multiplexer_7_out, multiplexer_8_out, multiplexer_9_out, multiplexer_10_out;

  // Probe on forwarding_unit_1_forward
  Forwarding_Unit forwarding_unit_1 (
    .Ex_M_We(Ex_Mem_WE), .Ex_M_Rd(Ex_Mem_Rd), .M_WB_We(Mem_WB_WE), .M_Wb_Rd(Mem_WB_Rd), .Id_Ex_Ra_b(Rt),
    .Forward(forwarding_unit_1_forward));
  Multiplexer #(.select(2), .width(32), .enable("false")) multiplexer_1 (
    .in0(A), .in1(Mem_D), .in2(WB_D), .in3(Mem_D), .out(A_t), .sel(forwarding_unit_2_forward));
  Multiplexer #(.select(2), .width(32), .enable("false")) multiplexer_2 (
    .in0(B), .in1(Mem_D), .in2(WB_D), .in3(Mem_D), .out(Store), .sel(forwarding_unit_1_forward));
  Forwarding_Unit forwarding_unit_2 (
    .Ex_M_We(Ex_Mem_WE), .Ex_M_Rd(Ex_Mem_Rd), .M_WB_We(Mem_WB_WE), .M_Wb_Rd(Mem_WB_Rd), .Id_Ex_Ra_b(Rs),
    .Forward(forwarding_unit_2_forward));
  // Probe on A_t
  Multiplexer #(.enable("false")) multiplexer_3 (.in0(A_t[31]), .in1(not_1_out), .out(multiplexer_3_out), .sel(LT_GE));
  not not_1 (not_1_out, A_t[31]);
  assign LTGEOut = {{31{1'b0}}, multiplexer_3_out};  // Bit_Extender bit_extender_1
  Multiplexer #(.width(32), .enable("false")) multiplexer_4 (
    .in0(Immediate), .in1(Store), .out(multiplexer_4_out), .sel(B_or_Immediate));
  Comparator #(.width(32), .mode("unsigned")) comparator_1 (
    .a(A_t), .b(multiplexer_4_out), .lt(comparator_1_lt));  // open: gt, eq
  Comparator #(.width(32)) comparator_2 (.a(A_t), .b(multiplexer_4_out), .lt(comparator_2_lt));  // open: gt, eq
  // Mips_ALU mips_alu_1: pin names not known; wires that end beside it: A_t, multiplexer_4_out, ALU_Op, mips_alu_1_p4, mips_alu_1_p5
  Multiplexer #(.width(5), .enable("false")) multiplexer_5 (
    .in0(multiplexer_6_out), .in1(A_t[4:0]), .out(mips_alu_1_p4), .sel(whichSA));
  Multiplexer #(.width(5), .enable("false")) multiplexer_6 (
    .in0(Immediate[10:6]), .in1(5'b10000), .out(multiplexer_6_out), .sel(and_2_out));
  assign bit_extender_2_out = {{31{1'b0}}, comparator_1_lt};  // Bit_Extender bit_extender_2
  assign bit_extender_3_out = {{31{1'b0}}, comparator_2_lt};  // Bit_Extender bit_extender_3
  Multiplexer #(.width(32), .enable("false")) multiplexer_7 (
    .in0(bit_extender_2_out), .in1(bit_extender_3_out), .out(multiplexer_7_out), .sel(ALU_Op[3]));
  and and_1 (MOVx, ALU_Op[3], ALU_Op[0]);
  and and_2 (and_2_out, ALU_Op[0], ~ALU_Op[2]);  // AND_Gate
  Multiplexer #(.width(32), .enable("false")) multiplexer_8 (
    .in0(mips_alu_1_p5), .in1(A_t), .out(multiplexer_8_out), .sel(MOVx));
  and and_3 (eq_ne_cmd, ALU_Op[0], ~ALU_Op[2], ALU_Op[3]);  // AND_Gate
  and and_4 (SLTx, ALU_Op[2], ALU_Op[1], ALU_Op[0]);
  EqZero eqzero_1 (.A(Store), .EqZ(eqzero_1_eqz));
  xor xor_1 (xor_1_out, eqzero_1_eqz, ALU_Op[1]);
  Multiplexer #(.width(32), .enable("false")) multiplexer_9 (
    .in0(multiplexer_8_out), .in1(multiplexer_7_out), .out(multiplexer_9_out), .sel(SLTx));
  or or_1 (or_1_out, xor_1_out, ~eq_ne_cmd);  // OR_Gate
  Multiplexer #(.select(2), .width(32), .enable("false")) multiplexer_10 (
    .in0(multiplexer_9_out), .in1(multiplexer_9_out), .in2(mips_alu_1_p5), .in3(LTGEOut),
    .out(multiplexer_10_out), .sel({Is_Branch, WeirdBranch}));
  and and_5 (WE2, WE, or_1_out);
  Multiplexer #(.width(32), .enable("false")) multiplexer_11 (
    .in0(multiplexer_10_out), .in1(PC_4), .out(D), .sel(or_2_out));
  or or_2 (or_2_out, Is_JAL, Is_JALR);
  Multiplexer #(.width(5), .enable("false")) multiplexer_12 (.in0(Rt), .in1(Rd), .out(Dest), .sel(or_3_out));
  or or_3 (or_3_out, Is_R, Is_JAL);
  and and_6 (Zap, D[0], Is_Branch);
  assign bit_extender_4_out = {{14{Immediate[15]}}, {Immediate[15:0], 2'b00}};  // Bit_Extender bit_extender_4
  Adder #(.width(32)) adder_1 (.a(bit_extender_4_out), .b(PC_4), .out(target));  // open: cin, cout

  assign Is_Branch_2 = Is_Branch;
  assign L_S_2 = L_S;
  assign Mem_out = Mem_in;
  assign MemSel_2 = MemSel;
  assign Sign_Unsign_2 = Sign_Unsign;

  // Other names for the same wires on the sheet: a_t_t[4:0] = A_t[4:0]; _2nd_bit = ALU_Op[1]; MSB = ALU_Op[3];
  //   B_t[31:0] = Store; ID_Ex_Rb[4:0] = Rt; ID_Ex_WE = WE; imm[31:0] = Immediate; JAL = Is_JAL;
  //   target_t[31:0] = PC_4
endmodule

module Decode (
  input  Zap,
  input  [31:0] Op,
  input  Clock,
  input  NOP_JR,
  output whichSa,
  output WriteEn,
  output Is_JR,
  output Is_JALR,
  output LT_GE,
  output [4:0] Rt,
  output [4:0] Rs,
  output [3:0] ALU_Op,
  output [4:0] Rd,
  output Is_JI,
  output Is_Branch,
  output Is_JAL,
  output B_or_Immediate,
  output L_S,
  output Sign_Unsign,
  output WeirdBranch,
  output MemSel,
  output [31:0] Immediate,
  output Mem,
  output Is_R
);

  wire non_immediate_decode_1_enable, non_immediate_decode_1_l_s;
  wire [4:0] non_immediate_decode_1_rd;
  wire [31:0] A_q, multiplexer_1_out;

  Register #(.width(32)) A (.D(Op), .Q(A_q), .clk(Clock));  // open: en, clr
  Multiplexer #(.width(32), .enable("false")) multiplexer_1 (
    .in0(Op), .in1(A_q), .out(multiplexer_1_out), .sel(NOP_JR));
  and and_1 (L_S, ~Zap, non_immediate_decode_1_l_s);  // AND_Gate
  Non_Immediate_Decode non_immediate_decode_1 (
    .Is_JR(Is_JR), .Op(multiplexer_1_out), .Memory(Mem), .L_S(non_immediate_decode_1_l_s),
    .Sign_Unsign(Sign_Unsign), .MemSel(MemSel), .Is_JI(Is_JI), .whichSA(whichSa), .WeirdBranch(WeirdBranch),
    .Enable(non_immediate_decode_1_enable), .IS_JALR(Is_JALR), .rd(non_immediate_decode_1_rd), .LT_GE(LT_GE),
    .rt(Rt), .rs(Rs), .Control(ALU_Op), .IsR(Is_R), .Is_Branch(Is_Branch), .Is_JAL(Is_JAL));
  Immediate_Decode immediate_decode_1 (
    .IsR(Is_R), .Op(multiplexer_1_out), .BorImmediate(B_or_Immediate), .Immediate(Immediate));
  and and_2 (WriteEn, ~Zap, non_immediate_decode_1_enable);  // AND_Gate
  Multiplexer #(.width(5), .enable("false")) multiplexer_2 (
    .in0(non_immediate_decode_1_rd), .in1({5{1'b1}}), .out(Rd), .sel(Is_JAL));
endmodule

module Jump_Forwarding (
  input  [4:0] Id_Ex_Ra_b,
  input  Ex_M_We,
  input  [4:0] Ex_M_Rd,
  input  M_WB_We,
  input  [4:0] M_Wb_Rd,
  input  WB_We,
  input  [4:0] Wb_Rd,
  input  Is_JR,
  output [1:0] Forward,
  output NOP
);

  wire ex_mem_bypass_1_forward, mem_wb_bypass_1_forward, mem_wb_bypass_2_forward;

  Ex_Mem_Bypass ex_mem_bypass_1 (
    .Ex_M_We(Ex_M_We), .Ex_M_Rd(Ex_M_Rd), .Id_Ex_Ra_b(Id_Ex_Ra_b), .Forward(ex_mem_bypass_1_forward));
  Mem_WB_Bypass mem_wb_bypass_1 (
    .M_WB_WE(M_WB_We), .M_WB_Rd(M_Wb_Rd), .Id_Ex_Ra_b(Id_Ex_Ra_b), .Ex_Mem_We(Ex_M_We), .Ex_M_Rd(Ex_M_Rd),
    .Forward(mem_wb_bypass_1_forward));
  Mem_WB_Bypass mem_wb_bypass_2 (
    .M_WB_WE(WB_We), .M_WB_Rd(Wb_Rd), .Id_Ex_Ra_b(Id_Ex_Ra_b), .Ex_Mem_We(M_WB_We), .Ex_M_Rd(M_Wb_Rd),
    .Forward(mem_wb_bypass_2_forward));
  and and_1 (Forward[0], ex_mem_bypass_1_forward, Is_JR);
  and and_2 (Forward[1], mem_wb_bypass_2_forward, Is_JR);
  and and_3 (NOP, mem_wb_bypass_1_forward, Is_JR);
endmodule

module EqZero5 (
  input  [4:0] A,
  output EqZ
);

  and and_1 (EqZ, ~A[0], ~A[1], ~A[2], ~A[3], ~A[4]);  // AND_Gate
endmodule
